// Logisim project D_flip_flop.circ as structural Verilog: 2 circuits, main circuit main
module main (
  input  Hold_Input,
  input  Data_Input,
  output Q,
  output Q_hat
);

  wire and_1_out, and_2_out, not_1_out;

  not not_1 (not_1_out, Data_Input);
  and and_1 (and_1_out, not_1_out, Hold_Input);
  and and_2 (and_2_out, Hold_Input, Data_Input);
  nor nor_1 (Q, Q_hat, and_1_out);
  nor nor_2 (Q_hat, and_2_out, Q);
endmodule

module D_filp_flop_4bit (
  input  [3:0] Data_input,
  input  Hold_Input,
  output [3:0] Q,
  output [3:0] Q_hat
);

  main main_1 (.Hold_Input(Hold_Input), .Data_Input(Data_input[0]), .Q(Q[0]), .Q_hat(Q_hat[0]));
  main main_2 (.Hold_Input(Hold_Input), .Data_Input(Data_input[1]), .Q(Q[1]), .Q_hat(Q_hat[1]));
  main main_3 (.Hold_Input(Hold_Input), .Data_Input(Data_input[2]), .Q(Q[2]), .Q_hat(Q_hat[2]));
  main main_4 (.Hold_Input(Hold_Input), .Data_Input(Data_input[3]), .Q(Q[3]), .Q_hat(Q_hat[3]));
endmodule
